# Fritzing sketch Clock_v4 (saved by Fritzing 0.9.3b)
circuit board: 8.84881cm x 4.29453cm
circuit board: 8.84881cm x 4.29453cm
breadboards: 1

parts:
  Arduino1 = Arduino Mini (Rev5)
  R1 = Rotary Potentiometer (Small) [maximum_resistance=100kΩ package=THT]
  VCC1 = Battery
  LCD1 = LCD screen

nets:
  GND: Arduino1.GND, R1.leg1, VCC1.-, LCD1.VSS, LCD1.R/W
  N1: Arduino1.D2, LCD1.DB7
  N2: Arduino1.D3_PWM, LCD1.DB6
  N3: Arduino1.D4, LCD1.DB5
  N4: Arduino1.D5_PWM, LCD1.DB4
  5V: Arduino1.5V, R1.leg2, VCC1.+, LCD1.VDD
  N5: Arduino1.D12, LCD1.RS
  N6: Arduino1.D11_PWM, LCD1.E
  N7: R1.wiper, LCD1.V0

custom parts:
  LCD screen: A standard character display, usually with 2x16 characters. Comes in many colors.
