# Fritzing sketch capmeter (saved by Fritzing 0.9.3b)
circuit board: 8.46667cm x 5.64444cm
breadboards: 1

parts:
  Деталь1 = Arduino Nano (Rev3.0)
  R1 = Resistor [tolerance=±5% resistance=100k power=0.25W package=THT]
  R2 = Resistor [tolerance=±5% resistance=220 package=THT]
  C1 = Electrolytic Capacitor [capacitance=0.1mF package="100 mil [THT, electrolytic]"]
  Деталь2 = DeuLigne 1.1 - The Snootlab's LCD shield for Arduino

nets:
  GND: Деталь1.GND, C1.-, Деталь2.GND
  N1: Деталь1.D11/MOSI, R2.Pin_1
  N2: Деталь1.D12/MISO, R1.Pin_0
  5V: Деталь1.5V, Деталь2.+5V
  N3: Деталь1.A5, Деталь2.A5(CLK)
  N4: Деталь1.A4, Деталь2.A4(SDA)
  N5: Деталь1.A0, R1.Pin_1, R2.Pin_0, C1.+
